# Fritzing sketch wiring (saved by Fritzing 0.9.3b)

parts:
  Bauteil1 = Arduino Pro Mini (3.3V)
  Config-Taster = Momentary Switch [package=ksa_sealed_tac_switch]
  LED1 = LED - 3mm [color="Green (560nm)" package="3 mm [THT]"]
  R1 = Resistor [tolerance=±5% resistance=330 package=THT]
  Antenne_~8_3cm = CC1101 [part_number=CC1101]
  R2 = Resistor [tolerance=±5% resistance=330 package=THT]
  LED2 = LED - 3mm [color="Red (635nm)" package="3 mm [THT]"]

nets:
  N1: Bauteil1.GND, Config-Taster.4, LED1.cathode, Antenne_~8_3cm.2, LED2.cathode
  N2: Bauteil1.VCC, Antenne_~8_3cm.1
  N3: Bauteil1.SCK, Antenne_~8_3cm.4
  N4: Bauteil1.MISO, Antenne_~8_3cm.5
  N5: Bauteil1.MOSI, Antenne_~8_3cm.3
  N6: Bauteil1.D10, Antenne_~8_3cm.8
  N7: Bauteil1.D8, Config-Taster.3
  N8: Bauteil1.D5, R2.Pin_0
  N9: Bauteil1.D4, R1.Pin_0
  N10: Bauteil1.D2, Antenne_~8_3cm.7
  N11: LED1.anode, R1.Pin_1
  N12: R2.Pin_1, LED2.anode

notes:
  LED2 nur bei Verwendung von "DualStatusLed"
